// Logisim project ProjetoULA_Jessica_Guerzoni_1801.circ as structural Verilog: 17 circuits, main circuit ProjetoALU
module subt (
  input  in_1,
  input  in_2,
  output out_3,
  output out_4
);

  xor xor_1 (out_3, in_1, in_2);
  and and_1 (out_4, in_2, ~in_1);  // AND_Gate
endmodule

module Andd (
  input  [7:0] in_1,
  input  [7:0] in_2,
  output [7:0] out_3
);

  assign out_3 = in_1 & in_2;  // AND_Gate and_1, 8 bits wide
endmodule

module ou (
  input  [7:0] in_1,
  input  [7:0] in_2,
  output [7:0] out_3
);

  assign out_3 = in_1 | in_2;  // OR_Gate or_1, 8 bits wide
endmodule

module nott (
  input  [7:0] in_1,
  output [7:0] out_2
);

  assign out_2 = ~in_1;  // NOT_Gate not_1, 8 bits wide
endmodule

module ProjetoALU (
  input  [7:0] A,
  input  [7:0] B,
  input  [3:0] opcode,
  output [7:0] Saida
);

  wire [7:0] And__out_3, desloc_dir_out_2, desloc_esq_out_2, multiplicador_out_3, Not__out_2, not_or_out_3,
       NotAnd_out_3, ou__out_3, Somador__out_3, Subtrator__s, xnor__out_3, xor__out_3;

  subtrator Subtrator_ (.S(Subtrator__s), .B(B), .A(A));
  multi multiplicador (.out_3(multiplicador_out_3), .in_2(A), .in_1(B));
  desl2 desloc_dir (.out_2(desloc_dir_out_2), .in_1(A));
  notE NotAnd (.in_2(B), .out_3(NotAnd_out_3), .in_1(A));
  somador Somador_ (.out_3(Somador__out_3), .in_2(B), .A(A));
  nott Not_ (.in_1(B), .out_2(Not__out_2));
  ou ou_ (.in_1(B), .in_2(A), .out_3(ou__out_3));
  xnorr xnor_ (.in_2(A), .out_3(xnor__out_3), .in_1(B));
  desl4 desloc_esq (.out_2(desloc_esq_out_2), .in_1(A));
  xorr xor_ (.in_2(A), .out_3(xor__out_3), .in_1(B));
  Andd And_ (.out_3(And__out_3), .in_2(A), .in_1(B));
  notou not_or (.in_2(A), .out_3(not_or_out_3), .in_1(B));
  Multiplexer #(.select(4), .width(8), .enable("false")) multiplexer_1 (
    .in1(Subtrator__s), .in2(multiplicador_out_3), .in3({8{1'b0}}), .in4(desloc_dir_out_2),
    .in5(NotAnd_out_3), .in6({8{1'b0}}), .in7(Somador__out_3), .in8(Not__out_2), .in9(ou__out_3),
    .in10(xnor__out_3), .in11(desloc_esq_out_2), .in12(xor__out_3), .in13({8{1'b0}}), .in14(And__out_3),
    .in15(not_or_out_3), .out(Saida), .sel(opcode));  // open: in0
endmodule

module xorr (
  input  [7:0] in_1,
  input  [7:0] in_2,
  output [7:0] out_3
);

  assign out_3 = in_1 ^ in_2;  // XOR_Gate xor_1, 8 bits wide
endmodule

module notou (
  input  [7:0] in_1,
  input  [7:0] in_2,
  output [7:0] out_3
);

  wire [7:0] or_1_out;

  assign or_1_out = in_1 | in_2;  // OR_Gate or_1, 8 bits wide
  assign out_3 = ~or_1_out;  // NOT_Gate not_1, 8 bits wide
endmodule

module notE (
  input  [7:0] in_1,
  input  [7:0] in_2,
  output [7:0] out_3
);

  wire [7:0] and_1_out;

  assign and_1_out = in_1 & in_2;  // AND_Gate and_1, 8 bits wide
  assign out_3 = ~and_1_out;  // NOT_Gate not_1, 8 bits wide
endmodule

module xnorr (
  input  [7:0] in_1,
  input  [7:0] in_2,
  output [7:0] out_3
);

  assign out_3 = ~(in_1 ^ in_2);  // XNOR_Gate xnor_1, 8 bits wide
endmodule

module multi (
  input  [7:0] in_1,
  input  [7:0] in_2,
  output [7:0] out_3
);

  Multiplier multiplier_1 (.a(in_1), .b(in_2), .out(out_3));  // open: cin, cout
endmodule

module desl4 (
  input  [7:0] in_1,
  output [7:0] out_2
);

  Shifter shifter_1 (.in(in_1), .\dist (3'b100), .out(out_2));
endmodule

module desl2 (
  input  [7:0] in_1,
  output [7:0] out_2
);

  Shifter #(.shift("lr")) shifter_1 (.in(in_1), .\dist (3'b010), .out(out_2));
endmodule

module somacomp (
  input  A,
  input  B,
  input  Cin,
  output S,
  output Cout
);

  wire soma_1_out_3, soma_1_out_4, soma_2_out_4;

  soma soma_1 (.out_4(soma_1_out_4), .out_3(soma_1_out_3), .in_2(B), .in_1(A));
  soma soma_2 (.out_4(soma_2_out_4), .out_3(S), .in_2(Cin), .in_1(soma_1_out_3));
  or or_1 (Cout, soma_2_out_4, soma_1_out_4);
endmodule

module soma (
  input  in_1,
  input  in_2,
  output out_3,
  output out_4
);

  xor xor_1 (out_3, in_1, in_2);
  and and_1 (out_4, in_1, in_2);
endmodule

module somador (
  input  [7:0] A,
  input  [7:0] in_2,
  output [7:0] out_3
);

  wire somacomp_1_cout, somacomp_2_cout, somacomp_3_cout, somacomp_4_cout, somacomp_5_cout, somacomp_6_cout,
       somacomp_7_cout, somacomp_8_cout;

  somacomp somacomp_1 (.Cout(somacomp_1_cout), .S(out_3[7]), .Cin(somacomp_2_cout), .B(in_2[7]), .A(A[7]));
  somacomp somacomp_2 (.Cout(somacomp_2_cout), .S(out_3[6]), .Cin(somacomp_3_cout), .B(in_2[6]), .A(A[6]));
  somacomp somacomp_3 (.Cout(somacomp_3_cout), .S(out_3[5]), .Cin(somacomp_4_cout), .B(in_2[5]), .A(A[5]));
  somacomp somacomp_4 (.Cout(somacomp_4_cout), .S(out_3[4]), .Cin(somacomp_5_cout), .B(in_2[4]), .A(A[4]));
  somacomp somacomp_5 (.Cout(somacomp_5_cout), .S(out_3[3]), .Cin(somacomp_6_cout), .B(in_2[3]), .A(A[3]));
  somacomp somacomp_6 (.Cout(somacomp_6_cout), .S(out_3[2]), .Cin(somacomp_7_cout), .B(in_2[2]), .A(A[2]));
  somacomp somacomp_7 (.Cout(somacomp_7_cout), .S(out_3[1]), .Cin(somacomp_8_cout), .B(in_2[1]), .A(A[1]));
  somacomp somacomp_8 (.Cout(somacomp_8_cout), .S(out_3[0]), .Cin(1'b0), .B(in_2[0]), .A(A[0]));
  // also tied to GND on the sheet: somacomp_1_cout
endmodule

module subc (
  input  in_1,
  input  in_2,
  input  in_3,
  output out_4,
  output out_5
);

  wire subt_1_out_3, subt_1_out_4, subt_2_out_4;

  subt subt_1 (.out_4(subt_1_out_4), .out_3(subt_1_out_3), .in_2(in_2), .in_1(in_1));
  subt subt_2 (.out_4(subt_2_out_4), .out_3(out_4), .in_2(in_3), .in_1(subt_1_out_3));
  or or_1 (out_5, subt_2_out_4, subt_1_out_4);
endmodule

module subtrator (
  input  [7:0] A,
  input  [7:0] B,
  output [7:0] S
);

  wire subc_1_out_5, subc_2_out_5, subc_3_out_5, subc_4_out_5, subc_5_out_5, subc_6_out_5, subc_8_out_5,
       subc_9_out_5;

  subc subc_1 (.out_5(subc_1_out_5), .out_4(S[7]), .in_3(subc_2_out_5), .in_2(B[7]), .in_1(A[7]));
  subc subc_2 (.out_5(subc_2_out_5), .out_4(S[6]), .in_3(subc_3_out_5), .in_2(B[6]), .in_1(A[6]));
  subc subc_3 (.out_5(subc_3_out_5), .out_4(S[5]), .in_3(subc_4_out_5), .in_2(B[5]), .in_1(A[5]));
  subc subc_4 (.out_5(subc_4_out_5), .out_4(S[4]), .in_3(subc_5_out_5), .in_2(B[4]), .in_1(A[4]));
  subc subc_5 (.out_5(subc_5_out_5), .out_4(S[3]), .in_3(subc_6_out_5), .in_2(B[3]), .in_1(A[3]));
  subc subc_6 (.out_5(subc_6_out_5), .out_4(S[2]), .in_3(subc_8_out_5), .in_2(B[2]), .in_1(A[2]));
  subc subc_7 (.out_5(subc_6_out_5), .out_4(S[2]), .in_3(subc_8_out_5), .in_2(B[2]), .in_1(A[2]));
  subc subc_8 (.out_5(subc_8_out_5), .out_4(S[1]), .in_3(subc_9_out_5), .in_2(B[1]), .in_1(A[1]));
  subc subc_9 (.out_5(subc_9_out_5), .out_4(S[0]), .in_3(1'b0), .in_2(B[0]), .in_1(A[0]));
  // also tied to GND on the sheet: subc_1_out_5
endmodule
